# Fritzing sketch SequencialSwitch (saved by Fritzing 0.9.3b)
stripboards: 1

parts:
  J8 = female pin header, 1 pin [form="♀ (female)" part_number="gnd point"]
  C2 = Electrolytic Capacitor [capacitance=47µF voltage=35V package="100 mil [THT, electrolytic]"]
  C1 = Electrolytic Capacitor [capacitance=47µF voltage=35V package="100 mil [THT, electrolytic]"]
  SW1 = Toggle Switch [part_number="3 position switch" package=THT]
  S1 = Momentary Switch [part_number=stepSW package=tactile_switch_smd]
  S2 = Momentary Switch [part_number=resetSW package=tactile_switch_smd]
  Reset = 3.5mm Switch Jack [part_number=PJ301M-12]
  Step = 3.5mm Switch Jack [part_number=PJ301M-12]
  OI = 3.5mm Switch Jack [part_number=PJ301M-12]
  IO1 = 3.5mm Switch Jack [part_number=PJ301M-12]
  IO2 = 3.5mm Switch Jack [part_number=PJ301M-12]
  IO3 = 3.5mm Switch Jack [part_number=PJ301M-12]
  IO4 = 3.5mm Switch Jack [part_number=PJ301M-12]
  D1 = Diode [part_number=1N5819WS package=sod-323]
  D2 = Diode [part_number=1N5819WS package=sod-323]
  D3 = Diode [part_number=1N4148 package=sod523]
  D4 = Diode [part_number=1N4148 package=sod523]
  D8 = Diode [part_number=1N4148 package=sod523]
  D7 = Diode [part_number=1N4148 package=sod523]
  D6 = Diode [part_number=1N4148 package=sod523]
  D5 = Diode [part_number=1N4148 package=sod523]
  Q4 = PNP-Transistor [part_number=3904 package="SOT-23 [SMD]"]
  Q2 = PNP-Transistor [part_number=3904 package="SOT-23 [SMD]"]
  Q3 = PNP-Transistor [part_number=3904 package="SOT-23 [SMD]"]
  Q1 = PNP-Transistor [part_number=3904 package="SOT-23 [SMD]"]
  C3 = Ceramic Capacitor [capacitance=10nF voltage=35V package="0603 [SMD, multilayer]"]
  C4 = Ceramic Capacitor [capacitance=10nF voltage=35V package="0603 [SMD, multilayer]"]
  C5 = Ceramic Capacitor [capacitance=100nF voltage=35V package="0603 [SMD, multilayer]"]
  C6 = Ceramic Capacitor [capacitance=100nF voltage=35V package="0603 [SMD, multilayer]"]
  C7 = Ceramic Capacitor [capacitance=10nF voltage=35V package="0603 [SMD, multilayer]"]
  R9 = Resistor [tolerance=±1% resistance=1k package="0603 [SMD]"]
  R6 = Resistor [tolerance=±1% resistance=47k package="0603 [SMD]"]
  R8 = Resistor [tolerance=±1% resistance=47k package="0603 [SMD]"]
  R11 = Resistor [tolerance=±1% resistance=1k package="0603 [SMD]"]
  R13 = Resistor [tolerance=±1% resistance=1k package="0603 [SMD]"]
  R3 = Resistor [tolerance=±1% resistance=10k package="0603 [SMD]"]
  R10 = Resistor [tolerance=±1% resistance=1k package="0603 [SMD]"]
  R15 = Resistor [tolerance=±1% resistance=1k package="0603 [SMD]"]
  R2 = Resistor [tolerance=±1% resistance=10k package="0603 [SMD]"]
  R4 = Resistor [tolerance=±1% resistance=47k package="0603 [SMD]"]
  R7 = Resistor [tolerance=±1% resistance=10k package="0603 [SMD]"]
  R1 = Resistor [tolerance=±1% resistance=47k package="0603 [SMD]"]
  R5 = Resistor [tolerance=±1% resistance=10k package="0603 [SMD]"]
  R14 = Resistor [tolerance=±1% resistance=1k package="0603 [SMD]"]
  R12 = Resistor [tolerance=±1% resistance=1k package="0603 [SMD]"]
  IC1 = SO16 [chip_label=4017 package=SO]
  IC2 = SO16 [chip_label=DG412 package=SO]
  J9 = female pin header, 5 pins [form="♀ (female)"]
  -_GND_+1 = female pin header, 5 pins [form="♀ (female)"]

nets:
  GND: J8.pin1, C2.+, C1.-, Reset.Pin_1, Step.Pin_1, OI.Pin_1, IO1.Pin_1, IO2.Pin_1, IO3.Pin_1, IO4.Pin_1, Q4.2, Q2.2, Q3.2, Q1.2, C3.0, C4.0, C5.1, C6.1, C7.0, R6.Pin_1, R4.Pin_1, IC1.8, IC1.13, IC2.5, J9.pin2, J9.pin3, J9.pin4, -_GND_+1.pin2, -_GND_+1.pin3, -_GND_+1.pin4
  -12V: C2.-, D1.A, C3.1, IC2.4
  12V: C1.+, D2.C, C4.1, C7.1, R3.Pin_0, R15.Pin_0, R2.Pin_0, R7.Pin_0, R5.Pin_0, R14.Pin_0, IC1.16, IC2.12, IC2.13
  Tre: SW1.L1, IC1.7, IC2.8
  N1: SW1.COM, D6.A
  Uno: SW1.L2, IC1.2, IC2.16
  N2: S1.1, R14.Pin_1
  N3: S1.3, D8.A, C5.0
  N4: S2.1, R15.Pin_1
  N5: S2.3, D7.A, C6.0
  N6: Reset.Pin_3, R8.Pin_0
  N7: Step.Pin_3, R1.Pin_0
  N8: OI.Pin_3, R9.Pin_0
  N9: IO1.Pin_3, R10.Pin_0
  N10: IO2.Pin_3, R11.Pin_0
  N11: IO3.Pin_3, R12.Pin_0
  N12: IO4.Pin_3, R13.Pin_0
  N13: D1.C, J9.pin5, -_GND_+1.pin5
  N14: D2.A, J9.pin1, -_GND_+1.pin1
  N15: D3.A, Q1.1, R3.Pin_1
  CLK: D3.C, D8.C, R4.Pin_0, IC1.14
  N16: D4.A, Q4.1, R5.Pin_1
  RES: D4.C, D7.C, D6.C, D5.C, R6.Pin_0, IC1.15
  N17: D5.A, IC1.10
  N18: Q4.0, Q3.1, R7.Pin_1
  N19: Q2.0, R1.Pin_1
  N20: Q2.1, Q1.0, R2.Pin_1
  N21: Q3.0, R8.Pin_1
  OI: R9.Pin_1, IC2.2, IC2.7, IC2.10, IC2.15
  IO2: R11.Pin_1, IC2.14
  IO4: R13.Pin_1, IC2.6
  IO1: R10.Pin_1, IC2.3
  IO3: R12.Pin_1, IC2.11
  Zero: IC1.3, IC2.1
  Dos: IC1.4, IC2.9

custom parts:
  3.5mm Switch Jack: Thonkiconn 3.5mm switching Jack
